# Fritzing sketch controllerman (saved by Fritzing 0.9.3b)
breadboards: 2

parts:
  GLCD_128x1 = 128 x 64 Graphic LCD
  Part1 = Arduino Nano (Rev3.0)
  R2 = Resistor [tolerance=±5% resistance=100 package=THT]
  R3 = Resistor [tolerance=±5% resistance=100 package=THT]
  U2 = MIDI_CONN_FEMALE [package=din_5_female]
  R5 = Resistor [tolerance=±5% resistance=220 package=THT]
  R6 = Resistor [tolerance=±5% resistance=220 package=THT]
  S1 = Pushbutton [package=THT]
  S2 = Pushbutton [package=THT]
  S3 = Pushbutton [package=THT]
  S4 = Pushbutton [package=THT]
  S5 = Pushbutton [package=THT]
  S6 = Pushbutton [package=THT]
  VCC1 = Battery block 9V
  R7 = Resistor [tolerance=±5% resistance=220 package="0402 [SMD]"]
  MP1584EN_Board1 = MP1584EN Power Regulator Board [part_number=MP1584EN]
  LED1 = RGB LED (com. cathode, rgb) [package="5 mm [THT]"]
  R1 = Resistor [tolerance=±5% resistance=150 package=THT]

nets:
  N1: GLCD_128x1.1_Vss, GLCD_128x1.15_CS1, GLCD_128x1.20_K(-), LED1.common_cathode
  N2: GLCD_128x1.2_Vdd, Part1.5V, R6.Pin_0, R7.Pin_1
  N3: GLCD_128x1.4_D/I, Part1.D10
  N4: GLCD_128x1.5_R/W, Part1.D11/MOSI
  N5: GLCD_128x1.6_Enable, Part1.D13/SCK
  N6: GLCD_128x1.17_RST, Part1.D8
  N7: GLCD_128x1.19_A(+), R7.Pin_0
  N8: Part1.D1/TX, R5.Pin_0
  N9: Part1.GND, U2.NC1, S1.leg0, S2.leg0, S3.leg0, S4.leg0, S5.leg0, S6.leg0, MP1584EN_Board1.OUT_-
  N10: Part1.D5, R1.Pin_1
  N11: Part1.D6, R2.Pin_1
  N12: Part1.D9, R3.Pin_1
  N13: Part1.VIN, MP1584EN_Board1.OUT_+
  N14: Part1.A5, S6.leg1
  N15: Part1.A4, S5.leg1
  N16: Part1.A3, S4.leg1
  N17: Part1.A2, S3.leg1
  N18: Part1.A1, S2.leg1
  N19: Part1.A0, S1.leg1
  N20: R2.Pin_0, LED1.green_anode
  N21: R3.Pin_0, LED1.blue_anode
  N22: U2.MIDI_IN, R5.Pin_1
  N23: U2.MIDI_OUT, R6.Pin_1
  N24: VCC1.-, MP1584EN_Board1.IN_-
  N25: VCC1.+, MP1584EN_Board1.IN_+
  N26: LED1.red_anode, R1.Pin_0

custom parts:
  MP1584EN Power Regulator Board: The MP1584EN is a high frequency step-down switching regulator. The input voltage range is 4.5V to 28V. The output voltage is set by the board's potentiometer.
